# Fritzing sketch button_led (saved by Fritzing 0.9.3b)

parts:
  Raspberry_Pi_1 = Raspberry Pi 3 [part_number=RPI-3-V1.2]
  Part1 = KY-004 Key Switch Module [package="Breakout board"]
  Part2 = KY-016 RGB Full Color LED Module [package="Breakout board"]

nets:
  N1: Raspberry_Pi_1.GND, Part1.-, Part2.-
  N2: Raspberry_Pi_1.GIPO18, Part2.R
  N3: Raspberry_Pi_1.GIPO15, Part1.S

notes:
  S : Signal/Data
  - : Ground
  - : Ground
  B : Blue
  G : Green
  R : Red

custom parts:
  KY-004 Key Switch Module: Arduino Key Switch Module Keyes KY-004 is a push button that will output a high signal when pressed.
  KY-016 RGB Full Color LED Module: KY-016 Arduino full color 5mm RGB LED, different colors can be obtained by mixing the three primary colors.
