# Fritzing sketch buzzer (saved by Fritzing 0.9.3b)

parts:
  Raspberry_Pi_1 = Raspberry Pi 3 [part_number=RPI-3-V1.2]
  Part1 = KY-012 Active Buzzer Module [package="Breakout board"]

nets:
  N1: Raspberry_Pi_1.GPIO18, Part1.-
  N2: Raspberry_Pi_1.GND, Part1.S

notes:
  - : Ground
  S : Signal/Data

custom parts:
  KY-012 Active Buzzer Module: Active Piezoelectric Buzzer Module Keyes KY-012, it produces single-tone sound when signal is high.
