# Fritzing sketch ds18_temp (saved by Fritzing 0.9.3b)

parts:
  Raspberry_Pi_1 = Raspberry Pi 3 [part_number=RPI-3-V1.2]
  DS1 = DS18B20 1-Wire Temperature Sensor [part_number=DS18B20]

nets:
  N1: Raspberry_Pi_1.3v3, DS1.DQ
  N2: Raspberry_Pi_1.GIPO4, DS1.VDD

notes:
  G = Ground
  R = 3.3v In
  Y = Data
  R = Pin 1
  Y = Pin 7
  G = Pin 9
