# Fritzing sketch rgbled (saved by Fritzing 0.9.3b)

parts:
  Raspberry_Pi_1 = Raspberry Pi 3 [part_number=RPI-3-V1.2]
  Part3 = KY-016 RGB Full Color LED Module [package="Breakout board"]

nets:
  N1: Raspberry_Pi_1.GPIO18, Part3.R
  N2: Raspberry_Pi_1.GND, Part3.-

notes:
  R : Red Cathode
  G : Green Cathode
  B : Blue Cathode
  - : Ground/Common

custom parts:
  KY-016 RGB Full Color LED Module: KY-016 Arduino full color 5mm RGB LED, different colors can be obtained by mixing the three primary colors.
